// Logisim project RISC_V_CPU_Projeto_1.circ as structural Verilog
module main (
  input  [4:0] in_1,
  input  in_2
);

  wire alu_1_flag_zero, and_1_out, clock_1_out, d_ff_1_q, exmem_1_zero_out, harzard_1_stall,
       multiplexer_10_out, not_1_out, or_2_out;
  wire [1:0] forward_1_forward_a, forward_1_forward_b, or_1_out, unidade_controle_1_aluop,
       unidade_controle_1_alusrc, unidade_controle_1_regsrc;
  wire [2:0] exmem_1_wb_out, idex_1_wb_out, memwb_1_wb_out, multiplexer_5_out;
  wire [2:2] unidade_controle_1_regwrite;
  wire [3:0] alu_controle_1_controle_alu, idex_1_alucontrol_out, idex_1_ex_out, ifid_1_instrucao_out_6,
       multiplexer_4_out;
  wire [4:0] exmem_1_mem_out, exmem_1_wbadd_out, idex_1_rs1_out, idex_1_rs2_out, idex_1_wbadd_out,
       ifid_1_instrucao_out, ifid_1_instrucao_out_2, ifid_1_instrucao_out_5, memwb_1_wbadd_out;
  wire [5:0] idex_1_mem_out, multiplexer_3_out, unidade_controle_1_memread;
  wire [6:0] ifid_1_instrucao_out_4;
  wire [7:0] counter_1_q;
  wire [31:0] alu_1_resultado, exmem_1_alu_out, exmem_1_pc4_out, exmem_1_pc_out, exmem_1_read2_out,
       gerador_imediato_1_imm, idex_1_immgen_out, idex_1_pc4_out, idex_1_pc_out, idex_1_read1_out,
       idex_1_read2_out, ifid_1_out_pc, ifid_1_pc4_out, memwb_1_alu_out, memwb_1_pc4_out, memwb_1_pci_out,
       memwb_1_read_out, multiplexer_1_out, multiplexer_2_out, multiplexer_6_out, multiplexer_7_out,
       multiplexer_8_out, multiplexer_9_out, multiplexer_11_out, pc_1_pc_out, ram_1_dout,
       register_file_1_outregmanual, register_file_1_saida_a, register_file_1_saida_b, rom_1_data,
       somador_1_s, somador_2_s;
  wire [31:25] ifid_1_instrucao_out_3;

  Clock clock_1 (.out(clock_1_out));
  Multiplexer #(.width(32)) multiplexer_1 (
    .in0(multiplexer_2_out), .in1(somador_1_s), .out(multiplexer_1_out), .sel(d_ff_1_q));  // open: en
  D_Flip_Flop d_ff_1 (.D(1'b0), .clk(clock_1_out), .Q(d_ff_1_q));  // open: Qn, preset, reset
  Counter counter_1 (.Q(counter_1_q), .clk(clock_1_out), .clr(in_2));  // open: load, D, count, carry, up
  PC pc_1 (
    .clk(counter_1_q[0]), .reset(in_2), .PC_in(multiplexer_1_out), .WriteEnableL(harzard_1_stall),
    .PC_out(pc_1_pc_out));
  ROM #(.addrWidth(24), .dataWidth(32)) rom_1 (.addr(pc_1_pc_out[23:0]), .data(rom_1_data));
  Somador somador_1 (.A(pc_1_pc_out), .B(32'h1), .S(somador_1_s));
  IFID ifid_1 (
    .clk(counter_1_q[0]), .In_PC(pc_1_pc_out), .PC4_In(somador_1_s), .WriteEnable_IFID(harzard_1_stall),
    .instrucao_In(rom_1_data), .Out_PC(ifid_1_out_pc), .PC4_Out(ifid_1_pc4_out),
    .instrucao_Out({ifid_1_instrucao_out_3[31], ifid_1_instrucao_out_6[3], ifid_1_instrucao_out_3[29:25], ifid_1_instrucao_out, ifid_1_instrucao_out_2, ifid_1_instrucao_out_6[2:0], ifid_1_instrucao_out_5, ifid_1_instrucao_out_4}));
  // Probe on {ifid_1_instrucao_out_3[31], ifid_1_instrucao_out_6[3], ifid_1_instrucao_out_3[29:25], ifid_1_instrucao_out, ifid_1_instrucao_out_2, ifid_1_instrucao_out_6[2:0], ifid_1_instrucao_out_5, ifid_1_instrucao_out_4}
  Harzard harzard_1 (
    .clk(clock_1_out), .MemReadEX(idex_1_mem_out[0]), .RDEX(idex_1_wbadd_out),
    .RSrc1(ifid_1_instrucao_out_2), .RSrc2(ifid_1_instrucao_out), .stall(harzard_1_stall));
  // Probe on register_file_1_outregmanual
  Register_File register_file_1 (
    .\input (multiplexer_11_out), .selRegManual(in_1), .WriteEnable(memwb_1_wb_out[2]),
    .selRegA(ifid_1_instrucao_out_2), .selRegB(ifid_1_instrucao_out), .selWriteReg(memwb_1_wbadd_out),
    .clk(clock_1_out), .saida_A(register_file_1_saida_a), .saida_B(register_file_1_saida_b),
    .outRegManual(register_file_1_outregmanual));
  Gerador_Imediato gerador_imediato_1 (
    .instrucao({ifid_1_instrucao_out_3[31], ifid_1_instrucao_out_6[3], ifid_1_instrucao_out_3[29:25], ifid_1_instrucao_out, ifid_1_instrucao_out_2, ifid_1_instrucao_out_6[2:0], ifid_1_instrucao_out_5, ifid_1_instrucao_out_4}),
    .imm(gerador_imediato_1_imm));
  Unidade_Controle unidade_controle_1 (
    .opcode(ifid_1_instrucao_out_4), .AluSrc(unidade_controle_1_alusrc[0]),
    .blockA(unidade_controle_1_alusrc[1]), .RegWrite(unidade_controle_1_regwrite[2]),
    .MemRead(unidade_controle_1_memread[0]), .MemWrite(unidade_controle_1_memread[1]),
    .Branch(unidade_controle_1_memread[2]), .BranchNotEq(unidade_controle_1_memread[3]),
    .BrIncond(unidade_controle_1_memread[4]), .RegToPC(unidade_controle_1_memread[5]),
    .AluOp(unidade_controle_1_aluop), .RegSrc(unidade_controle_1_regsrc));
  Multiplexer #(.select(2), .width(32)) multiplexer_2 (
    .in0(somador_1_s), .in1(exmem_1_pc_out), .in2(exmem_1_alu_out), .in3(exmem_1_alu_out),
    .out(multiplexer_2_out), .sel(or_1_out));  // open: en
  Multiplexer #(.width(6)) multiplexer_3 (
    .in0(unidade_controle_1_memread), .in1({6{1'b0}}), .out(multiplexer_3_out), .sel(harzard_1_stall));  // open: en
  Multiplexer #(.width(4)) multiplexer_4 (
    .in0({unidade_controle_1_aluop, unidade_controle_1_alusrc}), .in1(4'b0000), .out(multiplexer_4_out),
    .sel(harzard_1_stall));  // open: en
  Multiplexer #(.width(3)) multiplexer_5 (
    .in0({unidade_controle_1_regwrite[2], unidade_controle_1_regsrc}), .in1(3'b000), .out(multiplexer_5_out),
    .sel(harzard_1_stall));  // open: en
  IDEX idex_1 (
    .clk(counter_1_q[0]), .PC_In(ifid_1_out_pc), .read1_In(register_file_1_saida_a),
    .read2_In(register_file_1_saida_b), .immGen_In(gerador_imediato_1_imm),
    .aluControl_In(ifid_1_instrucao_out_6), .wbAdd_In(ifid_1_instrucao_out_5), .WB_In(multiplexer_5_out),
    .Mem_In(multiplexer_3_out), .EX_In(multiplexer_4_out), .PC4_In(ifid_1_pc4_out),
    .rs1_In(ifid_1_instrucao_out_2), .rs2_In(ifid_1_instrucao_out), .PC_Out(idex_1_pc_out),
    .read1_Out(idex_1_read1_out), .read2_Out(idex_1_read2_out), .immGen_Out(idex_1_immgen_out),
    .aluControl_Out(idex_1_alucontrol_out), .wbAdd_Out(idex_1_wbadd_out), .WB_Out(idex_1_wb_out),
    .Mem_Out(idex_1_mem_out), .EX_Out(idex_1_ex_out), .PC4_Out(idex_1_pc4_out), .rs1_Out(idex_1_rs1_out),
    .rs2_Out(idex_1_rs2_out));
  Multiplexer #(.width(32)) multiplexer_6 (
    .in0(idex_1_read1_out), .in1({32{1'b0}}), .out(multiplexer_6_out), .sel(idex_1_ex_out[1]));  // open: en
  Multiplexer #(.width(32)) multiplexer_7 (
    .in0(idex_1_read2_out), .in1(idex_1_immgen_out), .out(multiplexer_7_out), .sel(idex_1_ex_out[0]));  // open: en
  Multiplexer #(.select(2), .width(32)) multiplexer_8 (
    .in0(multiplexer_7_out), .in1(multiplexer_11_out), .in2(exmem_1_alu_out), .out(multiplexer_8_out),
    .sel(forward_1_forward_b));  // open: in3, en
  Multiplexer #(.select(2), .width(32)) multiplexer_9 (
    .in0(multiplexer_6_out), .in1(multiplexer_11_out), .in2(exmem_1_alu_out), .out(multiplexer_9_out),
    .sel(forward_1_forward_a));  // open: in3, en
  Somador somador_2 (.A(idex_1_pc_out), .B(idex_1_immgen_out), .S(somador_2_s));
  ALU alu_1 (
    .A(multiplexer_9_out), .B(multiplexer_8_out), .controle(alu_controle_1_controle_alu),
    .resultado(alu_1_resultado), .flag_zero(alu_1_flag_zero));
  ALU_Controle alu_controle_1 (
    .Funct(idex_1_alucontrol_out), .AluOp(idex_1_ex_out[3:2]), .Controle_ALU(alu_controle_1_controle_alu));
  Forward forward_1 (
    .clk(clock_1_out), .RegWriteWB(memwb_1_wb_out[0]), .RegWriteMEM(exmem_1_wb_out[0]),
    .RSrc1(idex_1_rs1_out), .RSrc2(idex_1_rs2_out), .RDWB(memwb_1_wbadd_out), .RDMEM(exmem_1_wbadd_out),
    .forward_A(forward_1_forward_a), .forward_B(forward_1_forward_b));
  EXMEM exmem_1 (
    .clk(counter_1_q[0]), .soma_In(somador_2_s), .zero_In(alu_1_flag_zero), .alu_In(alu_1_resultado),
    .read2_In(idex_1_read2_out), .wbAdd_In(idex_1_wbadd_out), .WB_In(idex_1_wb_out), .Mem_In(idex_1_mem_out),
    .PC4_In(idex_1_pc4_out), .PC_Out(exmem_1_pc_out), .zero_Out(exmem_1_zero_out), .alu_Out(exmem_1_alu_out),
    .read2_Out(exmem_1_read2_out), .wbAdd_Out(exmem_1_wbadd_out), .WB_Out(exmem_1_wb_out),
    .Mem_Out({or_1_out[1], exmem_1_mem_out}), .PC4_Out(exmem_1_pc4_out));
  or or_1 (or_1_out[0], exmem_1_mem_out[4], and_1_out);
  and and_1 (and_1_out, or_2_out, multiplexer_10_out);
  or or_2 (or_2_out, exmem_1_mem_out[2], exmem_1_mem_out[3]);
  Multiplexer multiplexer_10 (
    .in0(exmem_1_zero_out), .in1(not_1_out), .out(multiplexer_10_out), .sel(exmem_1_mem_out[3]));  // open: en
  not not_1 (not_1_out, exmem_1_zero_out);
  RAM #(.addrWidth(24), .dataWidth(32)) ram_1 (
    .addr(exmem_1_alu_out[23:0]), .we(exmem_1_mem_out[1]), .oe(exmem_1_mem_out[0]), .clk(clock_1_out),
    .din(exmem_1_read2_out), .dout(ram_1_dout));
  MEMWB memwb_1 (
    .clk(counter_1_q[0]), .read_In(ram_1_dout), .alu_In(exmem_1_alu_out), .wbAdd_In(exmem_1_wbadd_out),
    .WB_In(exmem_1_wb_out), .PC4_In(exmem_1_pc4_out), .PCI_In(exmem_1_pc_out), .read_Out(memwb_1_read_out),
    .alu_Out(memwb_1_alu_out), .wbAdd_Out(memwb_1_wbadd_out), .WB_Out(memwb_1_wb_out),
    .PC4_Out(memwb_1_pc4_out), .PCI_Out(memwb_1_pci_out));
  Multiplexer #(.select(2), .width(32)) multiplexer_11 (
    .in0(memwb_1_alu_out), .in1(memwb_1_read_out), .in2(memwb_1_pc4_out), .in3(memwb_1_pci_out),
    .out(multiplexer_11_out), .sel(memwb_1_wb_out[1:0]));  // open: en

  // Notes on the sheet:
  //   contents of rom_1 (hex, n*v repeats v):
  //   9563
endmodule

// VHDL entity ALU, as the project stores it:
library IEEE;
use IEEE.STD_LOGIC_1164.all;
use IEEE.numeric_std.ALL;
use IEEE.std_logic_unsigned.all;

entity ALU is
    port(
    A, B       : in std_logic_vector(31 downto 0);           -- Entradas A e B de 32 bits
    controle   : in std_logic_vector(3 downto 0);            -- Entrada de controle de 4 bits
    resultado  : out std_logic_vector(31 downto 0);          -- Saída de resultado de 32 bits
    flag_zero  : out std_logic);                             -- Saída para sinalizar se o resultado é zero
end ALU;

architecture Behavioral of ALU is

signal zero_out   : std_logic_vector(32 downto 0);           -- Vetor para verificação de resultado zero
signal resultado_out : std_logic_vector(31 downto 0);        -- Vetor para armazenar o resultado da operação

begin
	
 resultado_out <= (A + B) WHEN controle = "0010" ELSE        -- Soma
    			   (A - B) WHEN controle = "0110" ELSE        -- Subtração
    			   (A XOR B) WHEN controle = "0101" ELSE      -- XOR (ou exclusivo)
    			   (A OR B) WHEN controle = "0001" ELSE       -- OR (ou)
    			   (A AND B) WHEN controle = "0000" ELSE      -- AND (e)
    			   (std_logic_vector(shift_left(unsigned(A), to_integer(unsigned(B))))) WHEN controle = "0011" ELSE   -- Shift Left 
    			   (std_logic_vector(shift_right(unsigned(A), to_integer(unsigned(B))))) WHEN controle = "0111";    -- Shift Right
        			
    resultado <= resultado_out;                                      -- Atribui o valor do resultado à saída result
    
    zero_out(0) <= '0';                                              -- Inicializa o primeiro bit de zero_out como '0'
    
    G2: for I in 1 to 32 generate
            zero_out(I) <= zero_out(I - 1) OR resultado_out(I - 1);  -- Verificação de resultado zero bit a bit
    end generate;
    
    zero <= NOT zero_out(32);      -- Sinaliza se o resultado é zero (se zero_out(32) for '0', zero é '1', caso contrário, zero é '0')

end Behavioral;

// VHDL entity ALU_Controle, as the project stores it:
library IEEE;
use IEEE.STD_LOGIC_1164.all;

entity ALU_Controle is
    port(
        Funct        : in std_logic_vector(3 downto 0);    -- Entrada de códigos de função da ALU (4 bits)
        AluOp        :  in std_logic_vector(1 downto 0);   -- Entrada de códigos de operação da ALU (2 bits)
        Controle_ALU : out std_logic_vector(3 downto 0)    -- Saída do controle da ALU (4 bits)
        );
end ALU_Controle;

architecture Behavioral of ALU_Controle is
begin

	Controle_ALU <= "0010" WHEN AluOp = "00" ELSE         -- Se AluOp for "00", Controle_ALU recebe "0010" (Operação: Soma)
			 "0110" WHEN AluOp = "01" ELSE              -- Se AluOp for "01", Controle_ALU recebe "0110" (Operação: Branch)
			 "0010" WHEN Funct = "0000" ELSE            -- Se Funct for "0000", Controle_ALU recebe "0010" (Operação: Adição)
			 "0110" WHEN Funct = "1000" ELSE            -- Se Funct for "1000", Controle_ALU recebe "0110" (Operação: Subtração)
			 "0011" WHEN Funct = "0001" ELSE            -- Se Funct for "0001", Controle_ALU recebe "0011" (Operação: Shift Left)
			 "0101" WHEN Funct = "0100" ELSE            -- Se Funct for "0100", Controle_ALU recebe "0101" (Operação: XOR)
			 "0111" WHEN Funct = "0101" ELSE            -- Se Funct for "0101", Controle_ALU recebe "0111" (Operação: Shift Right)
			 "0001" WHEN Funct = "0110" ELSE            -- Se Funct for "0110", Controle_ALU recebe "0001" (Operação: OR)
			 "0000" WHEN Funct = "0111";                -- Se Funct for "0111", Controle_ALU recebe "0000" (Operação: AND)
	 
end Behavioral;

// VHDL entity Unidade_Controle, as the project stores it:
library IEEE;
use IEEE.STD_LOGIC_1164.all;

entity Unidade_Controle is
    port(
        opcode                     : IN  std_logic_vector(6 downto 0);   -- Entrada do código de operação (7 bits)
        AluSrc, blockA, RegWrite   : OUT std_logic;                      -- Saída de sinais de controle individuais (1 bit cada)
        MemRead, MemWrite, Branch  : OUT std_logic;                      -- Saída de sinais de controle individuais (1 bit cada)
        BranchNotEq, BrIncond      : OUT std_logic;                      -- Saída de sinais de controle individuais (1 bit cada)
        RegToPC                    : OUT std_logic;                      -- Saída de sinal de controle (1 bit)
        AluOp, RegSrc              : OUT std_logic_vector(1 downto 0)    -- Saída de códigos de operação da ALU e seleção de registradores (2 bits cada)
        );
end Unidade_Controle;

architecture Behavioral of Unidade_Controle is
begin
    -- Processo que verifica o opcode e define os sinais de controle correspondentes
    process(opcode)
    begin
        IF (opcode = "0110011") THEN             -- R-Type sem imediato (add, sub, and, or, xor, slt)
            AluSrc      <= '0';                  -- Seleção de fonte para a ALU (0: A_i, 1: Immediato)
            blockA      <= '0';                  -- Seleção de origem do registrador A (0: rs1, 1: zero)
            RegWrite    <= '1';                  -- Habilita escrita no registrador destino
            MemRead     <= '0';                  -- Habilita leitura de memória
            MemWrite    <= '0';                  -- Habilita escrita na memória
            Branch      <= '0';                  -- Habilita desvio condicional
            AluOp       <= "10";                 -- Código de operação da ALU para R-Type (00: and, 01: or, 10: add, 11: sub)
            RegSrc      <= "00";                 -- Seleção de registradores para R-Type (00: rs1, 01: rs2, 10: rd, 11: zero)
            BranchNotEq <= '0';                  -- Habilita desvio condicional se as entradas forem diferentes
            BrIncond    <= '0';                  -- Habilita desvio incondicional
            RegToPC     <= '0';                  -- Seleção de registrador para atualizar o PC (0: PC+4, 1: rd)
        end IF;

        IF (opcode = "0010011") THEN             -- I-Type (addi, andi, ori, xori, slti)
            AluSrc      <= '1';                  -- Seleção de fonte para a ALU (0: A_i, 1: Immediato)
            blockA      <= '0';                  -- Seleção de origem do registrador A (0: rs1, 1: zero)
            RegWrite    <= '1';                  -- Habilita escrita no registrador destino
            MemRead     <= '0';                  -- Habilita leitura de memória
            MemWrite    <= '0';                  -- Habilita escrita na memória
            Branch      <= '0';                  -- Habilita desvio condicional
            AluOp       <= "11";                 -- Código de operação da ALU para I-Type (00: andi, 01: ori, 10: addi, 11: slti)
            RegSrc      <= "00";                 -- Seleção de registradores para I-Type (00: rs1, 01: rd, 10: zero)
            BranchNotEq <= '0';                  -- Habilita desvio condicional se as entradas forem diferentes
            BrIncond    <= '0';                  -- Habilita desvio incondicional
            RegToPC     <= '0';                  -- Seleção de registrador para atualizar o PC (0: PC+4, 1: rd)
        end IF;

        IF (opcode = "0100011") THEN             -- S-Type (sw)
            AluSrc      <= '1';                  -- Seleção de fonte para a ALU (0: A_i, 1: Immediato)
            blockA      <= '0';                  -- Seleção de origem do registrador A (0: rs1, 1: zero)
            RegWrite    <= '0';                  -- Habilita escrita no registrador destino
            MemRead     <= '0';                  -- Habilita leitura de memória
            MemWrite    <= '1';                  -- Habilita escrita na memória
            Branch      <= '0';                  -- Habilita desvio condicional
            AluOp       <= "00";                 -- Código de operação da ALU para S-Type (00: add)
            RegSrc      <= "00";                 -- Seleção de registradores para S-Type (00: rs1, 01: zero)
            BranchNotEq <= '0';                  -- Habilita desvio condicional se as entradas forem diferentes
            BrIncond    <= '0';                  -- Habilita desvio incondicional
            RegToPC     <= '0';                  -- Seleção de registrador para atualizar o PC (0: PC+4, 1: rd)
        end IF;

        IF (opcode = "1100111") THEN             -- SB-Type (beq)
            AluSrc      <= '0';                  -- Seleção de fonte para a ALU (0: A_i, 1: Immediato)
            blockA      <= '0';                  -- Seleção de origem do registrador A (0: rs1, 1: zero)
            RegWrite    <= '0';                  -- Habilita escrita no registrador destino
            MemRead     <= '0';                  -- Habilita leitura de memória
            MemWrite    <= '0';                  -- Habilita escrita na memória
            Branch      <= '1';                  -- Habilita desvio condicional
            AluOp       <= "01";                 -- Código de operação da ALU para SB-Type (01: sub)
            RegSrc      <= "00";                 -- Seleção de registradores para SB-Type (00: rs1, 01: rs2)
            BranchNotEq <= '0';                  -- Habilita desvio condicional se as entradas forem diferentes
            BrIncond    <= '0';                  -- Habilita desvio incondicional
            RegToPC     <= '0';                  -- Seleção de registrador para atualizar o PC (0: PC+4, 1: rd)
        end IF;

        IF (opcode = "1100011") THEN -- SB-Type (bne)
            AluSrc      <= '0';                  -- Seleção de fonte para a ALU (0: A_i, 1: Immediato)
            blockA      <= '0';                  -- Seleção de origem do registrador A (0: rs1, 1: zero)
            RegWrite    <= '0';                  -- Habilita escrita no registrador destino
            MemRead     <= '0';                  -- Habilita leitura de memória
            MemWrite    <= '0';                  -- Habilita escrita na memória
            Branch      <= '0';                  -- Habilita desvio condicional
            AluOp       <= "01";                 -- Código de operação da ALU para SB-Type (01: sub)
            RegSrc      <= "00";                 -- Seleção de registradores para SB-Type (00: rs1, 01: rs2)
            BranchNotEq <= '1';                  -- Habilita desvio condicional se as entradas forem diferentes
            BrIncond    <= '0';                  -- Habilita desvio incondicional
            RegToPC     <= '0';                  -- Seleção de registrador para atualizar o PC (0: PC+4, 1: rd)

// VHDL entity Gerador_Imediato, as the project stores it:
library IEEE;
use IEEE.STD_LOGIC_1164.all;
use IEEE.NUMERIC_STD.all;

entity Gerador_Imediato is
    port( 
        instrucao: in std_logic_vector(31 downto 0);   -- Entrada da instrução (32 bits)
        imm: out std_logic_vector(31 downto 0)         -- Saída do valor imediato gerado (32 bits)
        );
end Gerador_Imediato;

architecture Behavioral of Gerador_Imediato is

    signal opcode       : std_logic_vector(6 downto 0);                                         -- Sinal para armazenar o campo opcode da instrução (7 bits)
    signal imm_interno  : std_logic_vector(31 downto 0) := "00000000000000000000000000000000";  -- Valor imediato interno inicializado com zero

begin

    opcode <= instrucao(6 downto 0);  -- Extrai o campo opcode da instrução

    process(opcode)
    
    begin
        IF (opcode = "0010011" OR opcode = "1100110") THEN              -- Tipo I (load-immediate, jump-register)
            imm_interno(11 downto 0)  <= instrucao(31 downto 20);       -- Extrai o imediato de 11 bits
            imm_interno(31 downto 12) <= (others => instrucao(31));     -- Sinal extendido para os bits mais significativos
        ELSIF (opcode = "1110111" OR opcode = "0110111") THEN           -- Tipo U (lui, auipc)
            imm_interno(31 downto 12) <= instrucao(31 downto 12);       -- Extrai o imediato de 20 bits
        ELSIF (opcode = "0100011") THEN                                 -- Tipo S (store)
            imm_interno(11 downto 5)  <= instrucao(31 downto 25);       -- Extrai o imediato de 7 bits (5-11)
            imm_interno(4 downto 0)   <= instrucao(11 downto 7);        -- Extrai o imediato de 5 bits (0-4)
            imm_interno(31 downto 12) <= (others => instrucao(31));     -- Sinal extendido para os bits mais significativos
        ELSIF (opcode = "1100111" OR opcode = "1100011") THEN           -- Tipo SB (branch)
            imm_interno(12)           <= instrucao(31);                 -- Extrai o bit de imediato (12)
            imm_interno(11)           <= instrucao(7);                  -- Extrai o bit de imediato (11)
            imm_interno(10 downto 5)  <= instrucao(30 downto 25);       -- Extrai o imediato de 6 bits (5-10)
            imm_interno(4 downto 1)   <= instrucao(11 downto 8);        -- Extrai o imediato de 4 bits (1-4)
            imm_interno(31 downto 13) <= (others => instrucao(31));     -- Sinal extendido para os bits mais significativos
        ELSIF (opcode = "1101111") THEN                                 -- Tipo UJ (jump)
            imm_interno(20)           <= instrucao(31);                 -- Extrai o bit de imediato (20)
            imm_interno(19 downto 12) <= instrucao(19 downto 12);       -- Extrai o imediato de 8 bits (12-19)
            imm_interno(11)           <= instrucao(20);                 -- Extrai o bit de imediato (11)
            imm_interno(10 downto 1)  <= instrucao(30 downto 21);       -- Extrai o imediato de 10 bits (1-10)
        end IF;
    end process;

    imm <= imm_interno;  -- Define a saída como o valor imediato gerado

end Behavioral;

// VHDL entity PC, as the project stores it:
LIBRARY ieee;
USE ieee.std_logic_1164.all;

entity PC IS
  port (
    clk            : in  std_logic;                       -- Entrada do sinal de clock
    reset          : in  std_logic;                       -- Entrada do sinal de reset
    PC_in          : in  std_logic_vector(31 downto 0);   -- Entrada do valor atual do PC (contador de programa)
    WriteEnableL   : in std_logic;                        -- Entrada do sinal de habilitação de escrita no PC
    PC_out         : out std_logic_vector(31 downto 0)    -- Saída do valor atualizado do PC (contador de programa)
    );
end PC;

architecture Behavioral of PC is

begin

	
	process (clk, reset, writeEnableL)
	begin
		IF (rising_edge(clk)) THEN -- Detecta a subida do sinal de clock
			IF (PC_in = "UUUUUUUUUUUUUUUUUUUUUUUUUUUUUUUU") THEN   
				PC_out <= (others => '0');                        -- Se valor de pc for desconhecido, zera o valor do PC
			ELSIF (WriteEnableL = '1') THEN-- Verifica se o sinal de habilitação de escrita está desabilitado
				PC_out <= PC_in;-- Se estiver desabilitado, o PC mantém o valor atual(Stall)
			end IF;
		end IF;
		IF (reset = '1') THEN -- Detecta a ocorrência de um reset (sinal de reset em nível alto)
			PC_out <= (others => '0');-- Nesse caso, zera o valor do PC
		end IF;
	end process;

end Behavioral;

// VHDL entity Somador, as the project stores it:
library ieee;
use ieee.std_logic_1164.all;
use IEEE.std_logic_unsigned.all; -- Pacote para operações aritméticas com std_logic_vector

entity Somador IS
  port (
    A, B        : in  std_logic_vector(31 downto 0); -- Vetor de entrada exemplo A e B de 32 bits
    S           : out std_logic_vector(31 downto 0)  -- Vetor de saída exemplo S de 32 bits
    );
end Somador;

architecture Behavioral of Somador is

begin

S <= A + B; -- Saída S é a soma dos vetores de entrada A e B

end Behavioral;

// VHDL entity Register_File, as the project stores it:
library IEEE;
use IEEE.std_logic_1164.all;
use IEEE.numeric_std.all;

entity Register_File is
  port(
    saida_A        : out std_logic_vector(31 downto 0);    -- Saída A do registrador
    saida_B        : out std_logic_vector(31 downto 0);    -- Saída B do registrador
    input          : in  std_logic_vector(31 downto 0);    -- Entrada de dado para escrita no registrador
    selRegManual   : in  std_logic_vector(4 downto 0);     -- Seleção manual de um registrador de saída
    outRegManual   : out std_logic_vector(31 downto 0);    -- Saída do registrador selecionado manualmente
    WriteEnable    : in  std_logic;                        -- Sinal de habilitação de escrita no registrador
    selRegA        : in  std_logic_vector(4 downto 0);     -- Seleção do registrador A para leitura
    selRegB        : in  std_logic_vector(4 downto 0);     -- Seleção do registrador B para leitura
    selWriteReg    : in  std_logic_vector(4 downto 0);     -- Seleção do registrador para escrita
    clk            : in  std_logic                         -- Sinal de clock
    );
end Register_File;

architecture Behavioral of Register_File is

  type RegisterFile is array(0 to 31) of std_logic_vector(31 downto 0);
  signal registers : RegisterFile := 
   -- Valores iniciais dos registradores
   -- Os primeiros 32 registradores têm os valores pré-definidos como "00000000000000000000000000010000", "00000000000000000000000000000001", etc.
   -- Até o último registrador "00000000000000000000000000000000"
   ("00000000000000000000000000010000","00000000000000000000000000000001","00000000000000000000000000000000","00000000000000000000000000000000",
    "00000000000000000000000000000000","00000000000000000000000000000000","00000000000000000000000000000000","00000000000000000000000000000000",
    "00000000000000000000000000000000","00000000000000000000000000000000","00000000000000000000000000000000","00000000000000000000000000000000",
    "00000000000000000000000000000000","00000000000000000000000000000000","00000000000000000000000000000000","00000000000000000000000000000000",
    "00000000000000000000000000000000","00000000000000000000000000000000","00000000000000000000000000000000","00000000000000000000000000000000",
    "00000000000000000000000000000000","00000000000000000000000000000000","00000000000000000000000000000000","00000000000000000000000000000000",
    "00000000000000000000000000000000","00000000000000000000000000000000","00000000000000000000000000000000","00000000000000000000000000000000",
    "00000000000000000000000000000000","00000000000000000000000000000000","00000000000000000000000000000000","00000000000000000000000000000000");

begin

  RegFile : process (clk) is
  
  begin
    IF rising_edge(clk) THEN
      -- Leitura dos registradores A e B antes do bypass
      IF (registers(to_integer(unsigned(selRegA))) = "UUUUUUUUUUUUUUUUUUUUUUUUUUUUUUUU") THEN
      	saida_A <= (others => '0');  -- Se o valor for "UUUU..." (indeterminado), a saída A será "0000..."
      ELSE 
      	saida_A <= registers(to_integer(unsigned(selRegA)));  -- Caso contrário, a saída A será o valor do registrador selecionado
      end IF;
      IF (registers(to_integer(unsigned(selRegB))) = "UUUUUUUUUUUUUUUUUUUUUUUUUUUUUUUU") THEN
      	saida_B <= (others => '0');  -- Se o valor for "UUUU..." (indeterminado), a saída B será "0000..."
      ELSE
      	saida_B <= registers(to_integer(unsigned(selRegB)));  -- Caso contrário, a saída B será o valor do registrador selecionado
      end IF;
      -- Escrita e bypass
      IF WriteEnable = '1' THEN
        registers(to_integer(unsigned(selWriteReg))) <= input;  -- Escreve o valor da entrada no registrador selecionado
        IF selRegA = selWriteReg THEN  -- Bypass para leitura A
          saida_A <= input;  -- Se o registrador A é o mesmo selecionado para escrita, a saída A recebe o valor da entrada
        end IF;
        IF selRegB = selWriteReg THEN  -- Bypass para leitura B
          saida_B <= input;  -- Se o registrador B é o mesmo selecionado para escrita, a saída B recebe o valor da entrada
        end IF;
      end IF;
    end IF;
  end process;

  -- Seleção manual
  -- O valor de saída outRegManual recebe o valor do registrador selecionado manualmente (regSelManual)
  
  outRegManual <= registers(to_integer(unsigned(selRegManual)));
  
end Behavioral;

// VHDL entity IFID, as the project stores it:
library ieee;
use ieee.std_logic_1164.all;

entity IFID is
  port (
    clk                : in  std_logic;                            -- Entrada do sinal de clock
    In_PC              : in  std_logic_vector(31 downto 0);        -- Entrada do valor atual do PC (contador de programa)
    PC4_In	        : in  std_logic_vector(31 downto 0);        -- Entrada do valor do PC mais 4 (próxima instrução)
    WriteEnable_IFID   : in std_logic;                             -- Entrada do sinal de habilitação de escrita no IFID
    instrucao_In       : in  std_logic_vector(31 downto 0);        -- Entrada da instrução atual buscada na memória de instruções
    Out_PC             : out std_logic_vector(31 downto 0);        -- Saída do valor atual do PC (contador de programa)
    PC4_Out	        : out std_logic_vector(31 downto 0);        -- Saída do valor do PC mais 4 (próxima instrução)
    instrucao_Out      : out std_logic_vector(31 downto 0)         -- Saída da instrução atual buscada na memória de instruções
    );
end IFID;

architecture Behavioral of IFID is

signal sinal : std_logic_vector(95 downto 0);                  -- Registrador de 96 bits para armazenar os valores do IFID

begin
	
	process (clk, WriteEnable_IFID)
	begin
		IF (rising_edge(clk)) THEN                    -- Detecta a borda de subida do sinal de clock
			IF (WriteEnable_IFID = '0') THEN         -- Verifica se o sinal de habilitação de escrita está desabilitado
				sinal(31 downto 0) <= instrucao_In; -- Se estiver desabilitado, armazena a instrução atual no IFID
				sinal(63 downto 32) <= In_PC;       -- Armazena o valor atual do PC
				sinal(95 downto 64) <= PC4_In;      -- Armazena o valor do PC mais 4 (próxima instrução)
			end IF;
		end IF;
		IF (falling_edge(clk)) THEN                   -- Detecta a borda de descida do sinal de clock
			Out_PC <= sinal(63 downto 32);           -- Na borda de descida, coloca na saída o valor do PC atual
			instrucao_Out <= sinal(31 downto 0);     -- Coloca na saída a instrução armazenada no IFID
			PC4_Out <= sinal(95 downto 64);          -- Coloca na saída o valor do PC mais 4
		end IF;
	end PROCESS;

end Behavioral;

// VHDL entity IDEX, as the project stores it:
library ieee;
use ieee.std_logic_1164.all;

entity IDEX is
  port (
    clk            : in  std_logic;                     -- Entrada do sinal de clock
    PC_In          : in  std_logic_vector(31 downto 0); -- Entrada do valor atual do PC (contador de programa)
    read1_In       : in  std_logic_vector(31 downto 0); -- Entrada do valor lido do registrador 1
    read2_In       : in  std_logic_vector(31 downto 0); -- Entrada do valor lido do registrador 2
    immGen_In      : in  std_logic_vector(31 downto 0); -- Entrada do valor gerado pela unidade ImmGen
    aluControl_In  : in  std_logic_vector(3 downto 0);  -- Entrada do controle da ALU
    wbAdd_In       : in  std_logic_vector(4 downto 0);  -- Entrada do endereço do registrador de destino para escrita
    WB_In		    : in  std_logic_vector(2 downto 0);  -- Entrada da fonte de escrita no registrador de destino
    Mem_In 	    : in  std_logic_vector(5 downto 0);  -- Entrada do sinal de controle de escrita na memória de dados
    EX_In    	    : in  std_logic_vector(3 downto 0);  -- Entrada do sinal de controle de execução
    PC4_In	    : in  std_logic_vector(31 downto 0); -- Entrada do valor do PC mais 4 (próxima instrução)
    rs1_In	    : in  std_logic_vector(4 downto 0);  -- Entrada do endereço do registrador 1
    rs2_In	    : in  std_logic_vector(4 downto 0);  -- Entrada do endereço do registrador 2
                        
    PC_Out          : out std_logic_vector(31 downto 0); -- Saída do valor atual do PC (contador de programa)
    read1_Out	     : out std_logic_vector(31 downto 0); -- Saída do valor lido do registrador 1
    read2_Out       : out std_logic_vector(31 downto 0); -- Saída do valor lido do registrador 2
    immGen_Out      : out std_logic_vector(31 downto 0); -- Saída do valor gerado pela unidade ImmGen
    aluControl_Out  : out std_logic_vector(3 downto 0);  -- Saída do controle da ALU
    wbAdd_Out       : out std_logic_vector(4 downto 0);  -- Saída do endereço do registrador de destino para escrita
    WB_Out		: out std_logic_vector(2 downto 0);  -- Saída da fonte de escrita no registrador de destino
    Mem_Out 		: out std_logic_vector(5 downto 0);  -- Saída do sinal de controle de escrita na memória de dados
    EX_Out    	     : out std_logic_vector(3 downto 0);  -- Saída do sinal de controle de execução
    PC4_Out	     : out std_logic_vector(31 downto 0); -- Saída do valor do PC mais 4 (próxima instrução)
    rs1_Out	     : out std_logic_vector(4 downto 0);  -- Saída do endereço do registrador 1
    rs2_Out	     : out std_logic_vector(4 downto 0)   -- Saída do endereço do registrador 2
    );
end IDEX;


architecture Behavioral of IDEX is

signal idex_s : std_logic_vector(191 downto 0);         -- Registrador de 192 bits para armazenar os valores do IDEX

begin

	process (clk)
	begin 
		IF (rising_edge(clk)) THEN                     -- Detecta a borda de subida do sinal de clock
			idex_s(31 downto 0)    <= PC_n;           -- Armazena o valor atual do PC
			idex_s(63 downto 32)   <= read1_In;       -- Armazena o valor lido do registrador 1
			idex_s(95 downto 64)   <= read2_In;       -- Armazena o valor lido do registrador 2
			idex_s(127 downto 96)  <= immGen_In;      -- Armazena o valor gerado pela unidade ImmGen
			idex_s(131 downto 128) <= aluControl_In;  -- Armazena o controle da ALU
			idex_s(136 downto 132) <= wbAdd_In;       -- Armazena o endereço do registrador de destino para escrita
			idex_s(139 downto 137) <= WB_In;          -- Armazena a fonte de escrita no registrador de destino
			idex_s(145 downto 140) <= Mem_In;         -- Armazena o sinal de controle de escrita na memória de dados
			idex_s(149 downto 146) <= EX_In;          -- Armazena o sinal de controle de execução
			idex_s(181 downto 150) <= PC4_In;         -- Armazena o valor do PC mais 4 (próxima instrução)
			idex_s(186 downto 182) <= rs1_In;         -- Armazena o endereço do registrador 1
			idex_s(191 downto 187) <= rs2_In;         -- Armazena o endereço do registrador 2
		end IF;
		IF (falling_edge(clk)) THEN                    -- Detecta a borda de descida do sinal de clock
			PC_Out    <= idex_s(31 downto 0);         -- Na borda de descida, coloca na saída o valor do PC atual
			read1_Out  <= idex_s(63 downto 32);       -- Coloca na saída o valor lido do registrador 1
			read2_Out  <= idex_s(95 downto 64);       -- Coloca na saída o valor lido do registrador 2
			immGen_Out <= idex_s(127 downto 96);      -- Coloca na saída
			aluControl_Out <= idex_s(131 downto 128);
			wbAdd_Out <= idex_s(136 downto 132);
			WB_Out <= idex_s(139 downto 137);
			Mem_Out <= idex_s(145 downto 140);
			EX_Out <= idex_s(149 downto 146);
			PC4_Out <= idex_s(181 downto 150);
			rs1_Out <= idex_s(186 downto 182);
			rs2_Out <= idex_s(191 downto 187);
		end IF;
	end PROCESS;

	
end Behavioral;

// VHDL entity EXMEM, as the project stores it:
library ieee;
use ieee.std_logic_1164.all;

entity EXMEM is
  port (
    clk            : in std_logic;                       -- Entrada do sinal de clock
    soma_In        : in  std_logic_vector(31 downto 0);  -- Entrada do resultado da ALU
    zero_In        : in  std_logic;                      -- Entrada do sinal de zero da ALU
    alu_In         : in  std_logic_vector(31 downto 0);  -- Entrada da operação da ALU
    read2_In       : in  std_logic_vector(31 downto 0);  -- Entrada do valor lido do registrador 2
    wbAdd_In       : in  std_logic_vector(4 downto 0);   -- Entrada do endereço do registrador de destino para escrita
    WB_In		    : in  std_logic_vector(2 downto 0);   -- Entrada da fonte de escrita no registrador de destino
    Mem_In 	    : in  std_logic_vector(5 downto 0);   -- Entrada do sinal de controle de escrita na memória de dados
    PC4_In	    : in std_logic_vector(31 downto 0);   -- Entrada do valor do PC mais 4 (próxima instrução)
    PC_Out         : out std_logic_vector(31 downto 0);  -- Saída do valor atual do PC (contador de programa)
    zero_Out	    : out std_logic;                      -- Saída do sinal de zero da ALU
    alu_Out        : out std_logic_vector(31 downto 0);  -- Saída do resultado da ALU
    read2_Out      : out std_logic_vector(31 downto 0);  -- Saída do valor lido do registrador 2
    wbAdd_Out      : out std_logic_vector(4 downto 0);   -- Saída do endereço do registrador de destino para escrita
    WB_Out	    : out std_logic_vector(2 downto 0);   -- Saída da fonte de escrita no registrador de destino
    Mem_Out 	    : out std_logic_vector(5 downto 0);   -- Saída do sinal de controle de escrita na memória de dados
    PC4_Out	    : out std_logic_vector(31 downto 0)   -- Saída do valor do PC mais 4 (próxima instrução)
    );
end EXMEM;


architecture Behavioral of EXMEM is

signal exmem_s : std_logic_vector(142 downto 0);        -- Registrador de 143 bits para armazenar os valores do EXMEM

begin

	process (clk)
	begin
		IF (rising_edge(clk)) THEN                    -- Detecta a borda de subida do sinal de clock
			exmem_s(31 downto 0)   <= soma_In;       -- Armazena o resultado da ALU
			exmem_s(32)  <= zero_In;                 -- Armazena o sinal de zero da ALU
			exmem_s(64 downto 33)  <= alu_In;        -- Armazena a operação da ALU
			exmem_s(96 downto 65) <= read2_In;       -- Armazena o valor lido do registrador 2
			exmem_s(101 downto 97) <= wbAdd_In;      -- Armazena o endereço do registrador de destino para escrita
			exmem_s(104 downto 102) <= WB_In;        -- Armazena a fonte de escrita no registrador de destino
			exmem_s(110 downto 105) <= Mem_In;       -- Armazena o sinal de controle de escrita na memória de dados
			exmem_s(142 downto 111) <= PC4_In;       -- Armazena o valor do PC mais 4 (próxima instrução)
		end IF;
		IF (falling_edge(clk)) THEN                   -- Detecta a borda de descida do sinal de clock
			PC_Out    <=  exmem_s(31 downto 0);      -- Na borda de descida, coloca na saída o valor do PC atual
			zero_Out  <=  exmem_s(32);               -- Coloca na saída o sinal de zero da ALU
			alu_Out   <=  exmem_s(64 downto 33);     -- Coloca na saída o resultado da ALU
			read2_Out <=  exmem_s(96 downto 65);     -- Coloca na saída o valor lido do registrador 2
			wbAdd_Out <=  exmem_s(101 downto 97);    -- Coloca na saída o endereço do registrador de destino para escrita
			WB_Out    <=  exmem_s(104 downto 102);   -- Coloca na saída a fonte de escrita no registrador de destino
			Mem_Out   <=  exmem_s(110 downto 105);   -- Coloca na saída o sinal de controle de escrita na memória de dados
			PC4_Out   <=  exmem_s(142 downto 111);   -- Coloca na saída o valor do PC mais 4 (próxima instrução)
		end IF;
	end process;
	
end Behavioral;

// VHDL entity MEMWB, as the project stores it:
library ieee;
use ieee.std_logic_1164.all;

entity MEMWB is
  port (
    clk           : in  std_logic;                      -- Entrada do sinal de clock
    read_In       : in  std_logic_vector(31 downto 0);  -- Entrada do valor lido da memória ou resultado da ALU
    alu_In        : in  std_logic_vector(31 downto 0);  -- Entrada do resultado da operação da ALU
    wbAdd_In      : in  std_logic_vector(4 downto 0);   -- Entrada do endereço do registrador de destino para escrita
    WB_In		   : in  std_logic_vector(2 downto 0);   -- Entrada da fonte de escrita no registrador de destino
    PC4_In	   : in std_logic_vector(31 downto 0);   -- Entrada do valor do PC mais 4 (próxima instrução)
    PCI_In	   : in std_logic_vector(31 downto 0);   -- Entrada do valor do PC mais I (endereço de retorno para chamadas de função)                
    read_Out      : out std_logic_vector(31 downto 0);  -- Saída do valor lido da memória ou resultado da ALU
    alu_Out	   : out std_logic_vector(31 downto 0);  -- Saída do resultado da operação da ALU
    wbAdd_Out     : out std_logic_vector(4 downto 0);   -- Saída do endereço do registrador de destino para escrita
    WB_Out	   : out std_logic_vector(2 downto 0);   -- Saída da fonte de escrita no registrador de destino
    PC4_Out       : out std_logic_vector(31 downto 0);  -- Saída do valor do PC mais 4 (próxima instrução)
    PCI_Out	   : out std_logic_vector(31 downto 0)   -- Saída do valor do PC mais I (endereço de retorno para chamadas de função)
    );
end MEMWB;

architecture Behavioral of MEMWB is

signal memwb_s : std_logic_vector(135 downto 0);        -- Registrador de 136 bits para armazenar os valores do MEMWB

begin

	process (clk)
	begin
		IF (rising_edge(clk)) THEN                   -- Detecta a borda de subida do sinal de clock
			memwb_s(31 downto 0)   <= readIn;       -- Armazena o valor lido da memória ou resultado da ALU
			memwb_s(63 downto 32)  <= aluIn;        -- Armazena o resultado da operação da ALU
			memwb_s(68 downto 64)  <= wbAddIn;      -- Armazena o endereço do registrador de destino para escrita
			memwb_s(71 downto 69)  <= WBin;         -- Armazena a fonte de escrita no registrador de destino
			memwb_s(103 downto 72) <= pcPl4In;      -- Armazena o valor do PC mais 4 (próxima instrução)
			memwb_s(135 downto 104) <= pcPlIIn;     -- Armazena o valor do PC mais I (endereço de retorno para chamadas de função)
			
		end IF;
		IF (falling_edge(clk)) THEN                   -- Detecta a borda de descida do sinal de clock
			read_Out    <=  memwb_s(31 downto 0);    -- Na borda de descida, valor lido da memória ou resultado da ALU
			alu_Out     <=  memwb_s(63 downto 32);   -- Coloca na saída o resultado da operação da ALU
			wbAdd_Out   <=  memwb_s(68 downto 64);   -- Coloca na saída o endereço do registrador de destino para escrita
			WB_Out      <=  memwb_s(71 downto 69);   -- Coloca na saída a fonte de escrita no registrador de destino
			PC4_Out     <=  memwb_s(103 downto 72);  -- Coloca na saída o valor do PC mais 4 (próxima instrução)
			PCI_Out     <=  memwb_s(135 downto 104); -- Coloca na saída o valor do PC mais I(endereço de retorno)
		end IF;
	end PROCESS;

	
end Behavioral;

// VHDL entity Harzard, as the project stores it:
library IEEE;
use IEEE.STD_LOGIC_1164.all;

entity Harzard is 
	port( 
        clk 		        : in std_logic;                        -- Entrada do sinal de clock
        MemReadEX 	        : in std_logic;                        -- Sinal indicando leitura na memória (saída do estágio EX do pipeline)
        RDEX, RSrc1, RSrc2  : in std_logic_vector(4 downto 0);     -- Registradores de destino e fontes da instrução (saídas do estágio EX do pipeline)
        stall		        : out std_logic                        -- Saída que indica se um "stall" (atraso) deve ser aplicado
	);
end Harzard;

architecture Behavioral of Harzard is

	signal stall_interno : std_logic := '0';  -- Sinal interno que armazena o valor do stall

begin

	process(clk)
    begin
        IF ((MemReadEX = '1') AND ((RDEX = RSrc1) OR (RDEX = RSrc2))) THEN
            stall_interno <='1';  -- Se houver uma leitura na memória (MemReadEX = '1') e o resultado da EX estiver em RSrc1 ou RSrc2, aplica um stall
        end IF;
    end process;
    stall <= stall_interno;      -- Atribui o valor do sinal interno stall_interno à saída stall
    
end Behavioral;

// VHDL entity Forward, as the project stores it:
library IEEE;
use IEEE.STD_LOGIC_1164.all;

entity Forward is 
	port( 
	     clk					: in std_logic;                      -- Entrada do sinal de clock
	     RegWriteWB, RegWriteMEM 	: in std_logic;                      -- Sinais de escrita no registrador (saídas de MEM/WB e WB do pipeline)
	     RSrc1, RSrc2			: in std_logic_vector(4 downto 0);   -- Registradores fonte da instrução (saídas de ID/EX do pipeline)
	     RDWB, RDMEM			: in std_logic_vector(4 downto 0);   -- Registradores de destino (saídas de MEM/WB e EX/MEM do pipeline)
	     forward_A, forward_B	: out std_logic_vector(1 downto 0)   -- Saídas indicando os encaminhamentos para as fontes A e B
     );
end Forward;

architecture Behavioral of Forward is

	signal forwardA_interno, forwardB_interno : std_logic_vector(1 downto 0) := "00";   -- Sinais internos que armazenam o encaminhamento

begin
	process(clk)
    begin
        IF ((RegWriteMEM = '1') AND (NOT(RDMEM = "00000")) AND (RDMEM = RSrc1)) THEN
        	forwardA_interno <= "10";   -- Encaminha o valor do registrador de MEM/WB para a fonte A
        end IF;

        IF ((RegWriteMEM = '1') AND (NOT(RDMEM = "00000")) AND (RDMEM = RSrc2)) THEN
        	forwardB_interno <= "10";   -- Encaminha o valor do registrador de MEM/WB para a fonte B
        end IF;

        IF ((RegWriteWB = '1') AND (NOT(RDWB = "00000")) AND (RDWB = RSrc1)) THEN
        	forwardA_interno <= "01";   -- Encaminha o valor do registrador de WB para a fonte A
        end IF;

        IF ((RegWriteWB = '1') AND (NOT(RDWB = "00000")) AND (RDWB = RSrc2)) THEN
        	forwardB_interno <= "01";   -- Encaminha o valor do registrador de WB para a fonte B
        end IF;

    end process;

    forward_A <= forwardA_interno;   -- Atribui o valor do sinal interno forwardA_interno à saída forwardA
    forward_B <= forwardB_interno;   -- Atribui o valor do sinal interno forwardB_interno à saída forwardB
    
end Behavioral;
