// Logisim project RISC_V_CPU_Vetorial_Projeto_2.circ as structural Verilog
module main (
  input  [4:0] in_1,
  input  in_2
);

  wire alu_1_flag_zero, and_1_out, clock_1_out, d_ff_1_q, exmem_1_zero_out, multiplexer_5_out, not_1_out,
       or_2_out;
  wire [1:0] or_1_out, unidade_controle_1_aluop, unidade_controle_1_regsrc, unidade_controle_1_tamanho;
  wire [2:0] exmem_1_wb_out, idex_1_wb_out, memwb_1_wb_out;
  wire [2:2] unidade_controle_1_regwrite;
  wire [3:0] controle_alu_1_alu_controle, idex_1_alucontrol_out, ifid_1_instrucao_out_6;
  wire [4:0] exmem_1_mem_out, exmem_1_wbadd_out, idex_1_wbadd_out, ifid_1_instrucao_out_3,
       ifid_1_instrucao_out_4, ifid_1_instrucao_out_5, memwb_1_wbadd_out, unidade_controle_1_alusrc;
  wire [5:0] idex_1_mem_out, unidade_controle_1_memread;
  wire [6:0] idex_1_ex_out, ifid_1_instrucao_out_2;
  wire [7:0] counter_1_q;
  wire [31:0] alu_1_resultado, exmem_1_alu_out, exmem_1_pc4_out, exmem_1_pc_out, exmem_1_read2_out,
       gerador_imediato_1_imm, idex_1_immgen_out, idex_1_pc4_out, idex_1_pc_out, idex_1_read1_out,
       idex_1_read2_out, ifid_1_pc4_out, ifid_1_pc_out, memwb_1_alu_out, memwb_1_pc4_out, memwb_1_pci_out,
       memwb_1_read_out, multiplexer_1_out, multiplexer_2_out, multiplexer_3_out, multiplexer_4_out,
       multiplexer_6_out, pc_1_p1, ram_1_dout, register_file_1_regmanual_out, register_file_1_saida_a,
       register_file_1_saida_b, rom_1_data, somador_1_s, somador_2_s;
  wire [31:25] ifid_1_instrucao_out;

  Clock clock_1 (.out(clock_1_out));
  Multiplexer #(.width(32)) multiplexer_1 (
    .in0(multiplexer_2_out), .in1(somador_1_s), .out(multiplexer_1_out), .sel(d_ff_1_q));
  D_Flip_Flop d_ff_1 (.D(1'b0), .clk(clock_1_out), .Q(d_ff_1_q));  // open: Qn, preset, reset
  Counter counter_1 (.Q(counter_1_q), .clk(clock_1_out), .clr(in_2));  // open: load, D, count, carry, up
  // PC pc_1: pin names not known; wires that end beside it: pc_1_p1
  ROM #(.addrWidth(24), .dataWidth(32)) rom_1 (.addr(pc_1_p1[23:0]), .data(rom_1_data));
  Somador somador_1 (.A(pc_1_p1), .B(32'h1), .S(somador_1_s));
  IFID ifid_1 (
    .clk(counter_1_q[0]), .PC_In(pc_1_p1), .PC4_In(somador_1_s), .instrucao_In(rom_1_data),
    .PC_Out(ifid_1_pc_out), .PC4_Out(ifid_1_pc4_out),
    .instrucao_Out({ifid_1_instrucao_out[31], ifid_1_instrucao_out_6[3], ifid_1_instrucao_out[29:25], ifid_1_instrucao_out_4, ifid_1_instrucao_out_3, ifid_1_instrucao_out_6[2:0], ifid_1_instrucao_out_5, ifid_1_instrucao_out_2}));
  // Probe on {ifid_1_instrucao_out[31], ifid_1_instrucao_out_6[3], ifid_1_instrucao_out[29:25], ifid_1_instrucao_out_4, ifid_1_instrucao_out_3, ifid_1_instrucao_out_6[2:0], ifid_1_instrucao_out_5, ifid_1_instrucao_out_2}
  // Probe on register_file_1_regmanual_out
  Register_File register_file_1 (
    .\input (multiplexer_6_out), .sel_RegManual(in_1), .WriteEnable(memwb_1_wb_out[2]),
    .sel_RegA(ifid_1_instrucao_out_3), .sel_RegB(ifid_1_instrucao_out_4), .sel_WriteReg(memwb_1_wbadd_out),
    .clk(clock_1_out), .saida_A(register_file_1_saida_a), .saida_B(register_file_1_saida_b),
    .RegManual_Out(register_file_1_regmanual_out));
  Gerador_Imediato gerador_imediato_1 (
    .instrucao({ifid_1_instrucao_out[31], ifid_1_instrucao_out_6[3], ifid_1_instrucao_out[29:25], ifid_1_instrucao_out_4, ifid_1_instrucao_out_3, ifid_1_instrucao_out_6[2:0], ifid_1_instrucao_out_5, ifid_1_instrucao_out_2}),
    .imm(gerador_imediato_1_imm));
  Unidade_Controle unidade_controle_1 (
    .opcode(ifid_1_instrucao_out_2), .AluSrc(unidade_controle_1_alusrc[0]),
    .blockA(unidade_controle_1_alusrc[1]), .RegWrite(unidade_controle_1_regwrite[2]),
    .MemRead(unidade_controle_1_memread[0]), .MemWrite(unidade_controle_1_memread[1]),
    .Branch(unidade_controle_1_memread[2]), .BranchNotEq(unidade_controle_1_memread[3]),
    .BrIncond(unidade_controle_1_memread[4]), .RegToPC(unidade_controle_1_memread[5]),
    .modo(unidade_controle_1_alusrc[4]), .AluOp(unidade_controle_1_aluop),
    .RegSrc(unidade_controle_1_regsrc), .tamanho(unidade_controle_1_tamanho));
  Multiplexer #(.select(2), .width(32)) multiplexer_2 (
    .in0(somador_1_s), .in1(exmem_1_pc_out), .in2(exmem_1_alu_out), .in3(exmem_1_alu_out),
    .out(multiplexer_2_out), .sel(or_1_out));
  // Probe on gerador_imediato_1_imm
  IDEX idex_1 (
    .clk(counter_1_q[0]), .PC_In(ifid_1_pc_out), .read1_In(register_file_1_saida_a),
    .read2_In(register_file_1_saida_b), .immGen_In(gerador_imediato_1_imm),
    .aluControl_In(ifid_1_instrucao_out_6), .wbAdd_In(ifid_1_instrucao_out_5),
    .WB_In({unidade_controle_1_regwrite[2], unidade_controle_1_regsrc}), .Mem_in(unidade_controle_1_memread),
    .EX_In({unidade_controle_1_tamanho, unidade_controle_1_alusrc[4], unidade_controle_1_aluop, unidade_controle_1_alusrc[1:0]}),
    .PC4_In(ifid_1_pc4_out), .PC_Out(idex_1_pc_out), .read1_Out(idex_1_read1_out),
    .read2_Out(idex_1_read2_out), .immGen_Out(idex_1_immgen_out), .aluControl_Out(idex_1_alucontrol_out),
    .wbAdd_Out(idex_1_wbadd_out), .WB_Out(idex_1_wb_out), .Mem_Out(idex_1_mem_out), .EX_Out(idex_1_ex_out),
    .PC4_Out(idex_1_pc4_out));
  Multiplexer #(.width(32)) multiplexer_3 (
    .in0(idex_1_read1_out), .in1({32{1'b0}}), .out(multiplexer_3_out), .sel(idex_1_ex_out[1]));
  Multiplexer #(.width(32)) multiplexer_4 (
    .in0(idex_1_read2_out), .in1(idex_1_immgen_out), .out(multiplexer_4_out), .sel(idex_1_ex_out[0]));
  Somador somador_2 (.A(idex_1_pc_out), .B(idex_1_immgen_out), .S(somador_2_s));
  ALU alu_1 (
    .A(multiplexer_3_out), .B(multiplexer_4_out), .controle(controle_alu_1_alu_controle),
    .modo(idex_1_ex_out[4]), .tamanho(idex_1_ex_out[6:5]), .resultado(alu_1_resultado),
    .flag_zero(alu_1_flag_zero));
  Controle_ALU controle_alu_1 (
    .Funct(idex_1_alucontrol_out), .AluOp(idex_1_ex_out[3:2]), .ALU_Controle(controle_alu_1_alu_controle));
  EXMEM exmem_1 (
    .clk(counter_1_q[0]), .soma_In(somador_2_s), .zero_In(alu_1_flag_zero), .alu_In(alu_1_resultado),
    .read2_In(idex_1_read2_out), .wbAdd_In(idex_1_wbadd_out), .WB_In(idex_1_wb_out), .Mem_In(idex_1_mem_out),
    .PC4_In(idex_1_pc4_out), .PC_Out(exmem_1_pc_out), .zero_Out(exmem_1_zero_out), .alu_Out(exmem_1_alu_out),
    .read2_Out(exmem_1_read2_out), .wbAdd_Out(exmem_1_wbadd_out), .WB_out(exmem_1_wb_out),
    .Mem_out({or_1_out[1], exmem_1_mem_out}), .PC4_Out(exmem_1_pc4_out));
  or or_1 (or_1_out[0], exmem_1_mem_out[4], and_1_out);
  and and_1 (and_1_out, or_2_out, multiplexer_5_out);
  or or_2 (or_2_out, exmem_1_mem_out[2], exmem_1_mem_out[3]);
  Multiplexer multiplexer_5 (
    .in0(exmem_1_zero_out), .in1(not_1_out), .out(multiplexer_5_out), .sel(exmem_1_mem_out[3]));
  not not_1 (not_1_out, exmem_1_zero_out);
  RAM #(.addrWidth(24), .dataWidth(32)) ram_1 (
    .addr(exmem_1_alu_out[23:0]), .we(exmem_1_mem_out[1]), .oe(exmem_1_mem_out[0]), .clk(clock_1_out),
    .din(exmem_1_read2_out), .dout(ram_1_dout));
  MEMWB memwb_1 (
    .clk(counter_1_q[0]), .read_In(ram_1_dout), .alu_In(exmem_1_alu_out), .wbAdd_In(exmem_1_wbadd_out),
    .WB_In(exmem_1_wb_out), .PC4_In(exmem_1_pc4_out), .PCI_In(exmem_1_pc_out), .read_Out(memwb_1_read_out),
    .alu_Out(memwb_1_alu_out), .wbAdd_Out(memwb_1_wbadd_out), .WB_Out(memwb_1_wb_out),
    .PC4_Out(memwb_1_pc4_out), .PCI_Out(memwb_1_pci_out));
  Multiplexer #(.select(2), .width(32)) multiplexer_6 (
    .in0(memwb_1_alu_out), .in1(memwb_1_read_out), .in2(memwb_1_pc4_out), .in3(memwb_1_pci_out),
    .out(multiplexer_6_out), .sel(memwb_1_wb_out[1:0]));

  // Notes on the sheet:
  //   contents of rom_1 (hex, n*v repeats v):
  //   100180
endmodule

// VHDL entity ALU, as the project stores it:
library IEEE;
use IEEE.STD_LOGIC_1164.all;
use IEEE.numeric_std.all;
use IEEE.std_logic_unsigned.all;

entity ALU is
    port(
    A, B        : in std_logic_vector(31 downto 0);   -- Entradas A e B de 32 bits
    controle    : in std_logic_vector(3 downto 0);    -- Sinal de controle de 4 bits para selecionar a operação
    modo        : in std_logic;                       -- Modo de operação: 0 para operação única e 1 para operação vetorial
    tamanho     : in std_logic_vector(1 downto 0);    -- Tamanho do vetor de operações (usado no modo vetorial)
    resultado   : out std_logic_vector(31 downto 0);  -- Saída da operação única (modo 0)
    flag_zero   : out std_logic                       -- Sinal de saída indicando se o resultado é zero
    );
end ALU;

architecture Behavioral of ALU is

-- Declaração dos sinais internos da ALU
signal zero_out   : std_logic_vector(32 downto 0);
signal zero_vec   : std_logic_vector(32 downto 0);
signal resultado_out : std_logic_vector(31 downto 0);
signal resultado_vec : std_logic_vector(31 downto 0);
signal add_vec    : std_logic_vector(31 downto 0);
signal sub_vec    : std_logic_vector(31 downto 0);
signal shiftl_vec : std_logic_vector(31 downto 0);
signal shiftr_vec : std_logic_vector(31 downto 0);

signal A3116 	   : std_logic_vector(15 downto 0);
signal A1500 	   : std_logic_vector(15 downto 0);

signal A3124      : std_logic_vector(7 downto 0);
signal A2316      : std_logic_vector(7 downto 0);
signal A1508      : std_logic_vector(7 downto 0);
signal A0700      : std_logic_vector(7 downto 0);

signal A3128      : std_logic_vector(3 downto 0);
signal A2724      : std_logic_vector(3 downto 0);
signal A2320      : std_logic_vector(3 downto 0);
signal A1916      : std_logic_vector(3 downto 0);
signal A1512      : std_logic_vector(3 downto 0);
signal A1108      : std_logic_vector(3 downto 0);
signal A0704      : std_logic_vector(3 downto 0);
signal A0300      : std_logic_vector(3 downto 0);

signal intB       : integer;

begin

	-- Conversão da entrada B para inteiro para uso nas operações de deslocamento
	intB <= to_integer(unsigned(B));

	-- Divisão do sinal de entrada A para partes menores para cálculos vetoriais
	A3116 <= A(31 downto 16);
	A1500 <= A(15 downto 0);

	A3124 <= A(31 downto 24);
	A2316 <= A(23 downto 16);
	A1508 <= A(15 downto 8);
	A0700 <= A(7 downto 0);

	A3128 <= A(31 downto 28);
	A2724 <= A(27 downto 24);
	A2320 <= A(23 downto 20);
	A1916 <= A(19 downto 16);
	A1512 <= A(15 downto 12);
	A1108 <= A(11 downto 8);
	A0704 <= A(7 downto 4);
	A0300 <= A(3 downto 0);
	
	-- Cálculos das operações vetoriais com base no tamanho do vetor (vecSize)
	add_vec <= (A + B) WHEN tamanho = "11" ELSE
			 ((A3116 + B(31 downto 16)) & (A1500 + B(15 downto 0))) WHEN tamanho = "10" ELSE
			 ((A3124 + B(31 downto 24)) & (A2316 + B(23 downto 16)) & (A1508 + B(15 downto 8)) & (A0700 + B(7 downto 0))) WHEN tamanho = "01" ELSE
			 ((A3128 + B(31 downto 28)) & (A2724 + B(27 downto 24)) & (A2320 + B(23 downto 20)) & (A1916 + B(19 downto 16)) & (A1512 + B(15 downto 12)) & (A1108 + B(11 downto 8)) & (A0704 + B(7 downto 4)) & (A0300 + B(3 downto 0))) WHEN tamanho = "00";
	
	sub_vec <= (A - B) WHEN tamanho = "11" ELSE
			 ((A3116 - B(31 downto 16)) & (A1500 - B(15 downto 0))) WHEN tamanho = "10" ELSE
			 ((A3124 - B(31 downto 24)) & (A2316 - B(23 downto 16)) & (A1508 - B(15 downto 8)) & (A0700 - B(7 downto 0))) WHEN tamanho = "01" ELSE
			 ((A3128 - B(31 downto 28)) & (A2724 - B(27 downto 24)) & (A2320 - B(23 downto 20)) & (A1916 - B(19 downto 16)) & (A1512 - B(15 downto 12)) & (A1108 - B(11 downto 8)) & (A0704 - B(7 downto 4)) & (A0300 - B(3 downto 0))) WHEN tamanho = "00";
	
	-- Cálculos das operações de deslocamento vetoriais
	shiftl_vec <= (std_logic_vector(shift_left(unsigned(A), intB))) WHEN tamanho = "11" ELSE
			 ((std_logic_vector(shift_left(unsigned(A3116), intB))) & std_logic_vector(shift_left(unsigned(A1500), intB))) WHEN tamanho = "10" ELSE
			 ((std_logic_vector(shift_left(unsigned(A3124), intB))) & (std_logic_vector(shift_left(unsigned(A2316), intB))) & (std_logic_vector(shift_left(unsigned(A1508), intB))) & (std_logic_vector(shift_left(unsigned(A0700), intB)))) WHEN tamanho = "01" ELSE
			 ((std_logic_vector(shift_left(unsigned(A3128), intB))) & (std_logic_vector(shift_left(unsigned(A2724), intB))) & (std_logic_vector(shift_left(unsigned(A2320), intB))) & (std_logic_vector(shift_left(unsigned(A1916), intB))) & (std_logic_vector(shift_left(unsigned(A1512), intB))) & (std_logic_vector(shift_left(unsigned(A1108), intB))) & (std_logic_vector(shift_left(unsigned(A0704), intB))) & (std_logic_vector(shift_left(unsigned(A0300), intB)))) WHEN tamanho = "00";

	shiftr_vec <= (std_logic_vector(shift_right(unsigned(A), intB))) WHEN tamanho = "11" ELSE
			 ((std_logic_vector(shift_right(unsigned(A3116), intB))) & std_logic_vector(shift_right(unsigned(A1500), intB))) WHEN tamanho = "10" ELSE
			 ((std_logic_vector(shift_right(unsigned(A3124), intB))) & (std_logic_vector(shift_right(unsigned(A2316), intB))) & (std_logic_vector(shift_right(unsigned(A1508), intB))) & (std_logic_vector(shift_right(unsigned(A0700), intB)))) WHEN tamanho = "01" ELSE
			 ((std_logic_vector(shift_right(unsigned(A3128), intB))) & (std_logic_vector(shift_right(unsigned(A2724), intB))) & (std_logic_vector(shift_right(unsigned(A2320), intB))) & (std_logic_vector(shift_right(unsigned(A1916), intB))) & (std_logic_vector(shift_right(unsigned(A1512), intB))) & (std_logic_vector(shift_right(unsigned(A1108), intB))) & (std_logic_vector(shift_right(unsigned(A0704), intB))) & (std_logic_vector(shift_right(unsigned(A0300), intB)))) WHEN tamanho = "00";
	
	-- Seleção da operação de acordo com o sinal de controle
	resultado_vec <= add_vec WHEN controle = "0010" ELSE
			    sub_vec WHEN controle = "0110" ELSE
			    shiftl_vec WHEN controle = "0011" ELSE
			    shiftr_vec WHEN controle = "0111" ELSE
			    (others => '0');

	-- Seleção da operação no modo único ou vetorial (modo 0 ou 1)
    resultado_out <= (A + B) WHEN controle = "0010" ELSE
    			   (A - B) WHEN controle = "0110" ELSE
    			   (A XOR B) WHEN controle = "0101" ELSE
    			   (A OR B) WHEN controle = "0001" ELSE
    			   (A AND B) WHEN controle = "0000" ELSE
    			   (std_logic_vector(shift_left(unsigned(A), intB))) WHEN controle = "0011" ELSE
    			   (std_logic_vector(shift_right(unsigned(A), intB))) WHEN controle = "0111";
        			
    resultado <= resultado_out WHEN modo = '0' ELSE
    		    resultado_vec WHEN modo = '1';
    		    
    -- Cálculo dos sinais de saída zero para modo único e vetorial
    zero_out(0)<= '0';
    zero_vec(0) <= '0';
    G2: for I in 1 to 32 generate
            zero_out(I) <= zero_out(I - 1) OR resultado_out(I - 1);
            zero_vec(I) <= zero_vec(I - 1) OR resultado_vec(I - 1);
    end generate;
    
    flag_zero <= (NOT zero_out(32)) WHEN modo = '0' ELSE
    		  (NOT zero_vec(32)) WHEN modo = '1';
    		  
end Behavioral;

// VHDL entity Controle_ALU, as the project stores it:
library IEEE;
use IEEE.STD_LOGIC_1164.all;

entity Controle_ALU is
    port(
        Funct    : in std_logic_vector(3 downto 0);    -- Entrada que contém o código da função da ALU
        AluOp     : in std_logic_vector(1 downto 0);   -- Entrada que contém o código da operação da ALU
        ALU_Controle   : out std_logic_vector(3 downto 0)   -- Saída que contém o sinal de controle da ALU
        );
end Controle_ALU;

architecture Behavioral of Controle_ALU is

begin

	-- Lógica para gerar o sinal de controle (Control) com base nas entradas Functs e AluOp
ALU_Controle <= "0010" WHEN AluOp = "00" ELSE    -- Operação de adição
			 "0110" WHEN AluOp = "01" ELSE    -- Operação de subtração
			 "0010" WHEN Funct = "0000" ELSE  -- Funct = 0000, operação de adição
			 "0110" WHEN Funct = "1000" ELSE  -- Funct = 1000, operação de subtração
			 "0011" WHEN Funct = "0001" ELSE  -- Funct = 0001, operação de shift left
			 "0101" WHEN Funct = "0100" ELSE  -- Funct = 0100, operação de XOR
			 "0111" WHEN Funct = "0101" ELSE  -- Funct = 0101, operação de shift right
			 "0001" WHEN Funct = "0110" ELSE  -- Funct = 0110, operação de OR
			 "0000" WHEN Funct = "0111";      -- Funct = 0111, operação de AND
			 
	-- As combinações restantes de Functs e AluOp não têm uma operação específica definida.
	-- Caso nenhuma das condições acima seja satisfeita, o sinal de controle será "0000" (AND).
	
end Behavioral;

// VHDL entity Unidade_Controle, as the project stores it:
library IEEE;
use IEEE.STD_LOGIC_1164.all;

entity Unidade_Controle is
    port(
        opcode                     : in  std_logic_vector(6 downto 0);  -- Entrada que contém o opcode da instrução
        AluSrc, blockA, RegWrite 	: out std_logic;                     -- Sinais de controle da ALU
        MemRead, MemWrite, Branch  : out std_logic;                     -- Sinais de controle de memória
        BranchNotEq, BrIncond		: out std_logic;                     -- Sinais de controle para desvios condicionais e incondicionais
        RegToPC, modo			: out std_logic;                     -- Sinais de controle para modificação do PC (Contador de Programa)
        AluOp,RegSrc, tamanho		: out std_logic_vector(1 downto 0)   -- Sinais de controle adicionais para a ALU
        );
end Unidade_Controle;

architecture Behavioral of Unidade_Controle is

begin

	process(opcode)
	begin
	
	    -- Bloco de seleção para gerar os sinais de controle com base no opcode da instrução
	    IF (opcode = "0110011") THEN -- R-Type sem imediato
	        AluSrc      <= '0';
	        blockA      <= '0';
	        RegWrite    <= '1';
	        MemRead     <= '0';
	        MemWrite    <= '0';
	        Branch      <= '0';
	        AluOp       <= "10";
	        RegSrc      <= "00";
	        BranchNotEq <= '0';
	        BrIncond    <= '0';
	        RegToPC     <= '0';
	        modo        <= '0';     
	        tamanho     <= "00";
	    end IF;
	    
	    -- Mais blocos IF/THEN/ELSE para mapear os demais opcodes às operações e sinais de controle correspondentes.
	    -- Cada bloco IF/THEN/ELSE representa uma instrução diferente, definindo quais sinais de controle devem ser ativados
	    -- para cada tipo de instrução.

	end process;
	
end Behavioral;

// VHDL entity Gerador_Imediato, as the project stores it:
library IEEE;
use IEEE.STD_LOGIC_1164.all;
use IEEE.NUMERIC_STD.all;

entity Gerador_Imediato is
    Port( 
        instrucao: in std_logic_vector(31 downto 0); -- Entrada contendo a instrução de 32 bits
        imm: out std_logic_vector(31 downto 0)  -- Saída contendo o imediato de 32 bits
    );
end Gerador_Imediato;

architecture Behavioral of Gerador_Imediato is

    -- Declaração de sinais para armazenar o opcode e o imediato interno.
    signal opcode        : std_logic_vector(6 downto 0); 
    signal imm_interno   : std_logic_vector(31 downto 0) := "00000000000000000000000000000000"; -- Inicializa o imediato interno com valor '0'.

begin

    -- Extrai o opcode da instrução de entrada.
    opcode <= instrucao(6 downto 0);

    process(opcode)
    begin
        -- Bloco de seleção para gerar o imediato com base no opcode da instrução
       IF (opcode = "0010011" OR opcode = "1100110" OR opcode = "0000100" OR opcode = "0000101" OR opcode = "0000001") THEN -- I type
            imm_interno(11 downto 0)  <= instrucao(31 downto 20);     -- Bits 31:20 são copiados diretamente para os bits 11:0 do imediato
            imm_interno(31 downto 12) <= (others => instrucao(31));  -- O bit 31 é copiado para todos os bits 31:12 do imediato
        ELSIF (opcode = "1110111" OR opcode = "0110111" OR opcode = "0001000" OR opcode = "0001001" OR opcode = "0001010") THEN -- U type
            imm_interno(31 downto 12) <= instrucao(31 downto 12);    -- Bits 31:12 são copiados diretamente para os bits 31:12 do imediato
        ELSIF (opcode = "0100011") THEN -- S type
            imm_interno(11 downto 5) <= instrucao(31 downto 25);     -- Bits 31:25 são copiados diretamente para os bits 11:5 do imediato
            imm_interno(4 downto 0)  <= instrucao(11 downto 7);      -- Bits 11:7 são copiados diretamente para os bits 4:0 do imediato
            imm_interno(31 downto 12) <= (others => instrucao(31));  -- O bit 31 é copiado para todos os bits 31:12 do imediato
        ELSIF (opcode = "1100111" OR opcode = "1100011") THEN -- SB type
            imm_interno(12) <= instrucao(31);                       -- O bit 31 é copiado para o bit 12 do imediato
            imm_interno(11) <= instrucao(7);                        -- O bit 7 é copiado para o bit 11 do imediato
            imm_interno(10 downto 5) <= instrucao(30 downto 25);     -- Bits 30:25 são copiados diretamente para os bits 10:5 do imediato
            imm_interno(4 downto 1) <= instrucao(11 downto 8);       -- Bits 11:8 são copiados diretamente para os bits 4:1 do imediato
            imm_interno(31 downto 13) <= (others => instrucao(31));  -- O bit 31 é copiado para todos os bits 31:13 do imediato
        ELSIF (opcode = "1101111") THEN -- UJ type
            imm_interno(20) <= instrucao(31);                       -- O bit 31 é copiado para o bit 20 do imediato
            imm_interno(19 downto 12) <= instrucao(19 downto 12);    -- Bits 19:12 são copiados diretamente para os bits 19:12 do imediato
            imm_interno(11) <= instrucao(20);                       -- O bit 20 é copiado para o bit 11 do imediato
            imm_interno(10 downto 1) <= instrucao(30 downto 21);     -- Bits 30:21 são copiados diretamente para os bits 10:1 do imediato
        end IF;
    end process;

    -- Saída do imediato gerado.
    imm <= imm_interno;

end Behavioral;

// VHDL entity PC, as the project stores it:
library IEEE;
use IEEE.std_logic_1164.all;

entity PC is
  port (
    clk      : in  std_logic;                      -- Sinal de clock (entrada)
    reset    : in  std_logic;                      -- Sinal de reset (entrada)
    PC_In    : in  std_logic_vector(31 downto 0);  -- Dado de entrada de 32 bits (vetor de entrada)
    PC_Out   : in std_logic_vector(31 downto 0)    -- Dado de saída de 32 bits (vetor de saída)
  );
end PC;

architecture Behavioral of PC is

begin

	process (clk, reset)
	begin
	
		IF (rising_edge(clk)) THEN
			IF (PC_In = "UUUUUUUUUUUUUUUUUUUUUUUUUUUUUUUU") THEN
				-- Se a entrada for desconhecida (U), o dado de saída é zerado.
				PC_Out <= (others => '0');
			ELSE
				-- Caso contrário, copia o dado de entrada para a saída.
				PC_Out <= PC_In;
			end IF;
		end IF;
		IF (reset = '1') THEN
			-- Se o sinal de reset for '1', o dado de saída é zerado.
			PC_Out <= (others => '0');
		end IF;
	end process;
	
end Behavioral;

// VHDL entity Somador, as the project stores it:
library IEEE;
use IEEE.std_logic_1164.all;
use IEEE.std_logic_unsigned.all;

entity Somador is
  port (
    A, B : in  std_logic_vector(31 downto 0); -- Números de entrada de 32 bits (vetor de entrada)
    S    : out std_logic_vector(31 downto 0)  -- Resultado da soma (vetor de saída)
  );
end Somador;

architecture Behavioral of Somador is

begin

  -- O sinal de saída Z recebe a soma dos valores de A e B.
  S <= A + B;

end Behavioral;

// VHDL entity Register_File, as the project stores it:
library ieee;
use ieee.std_logic_1164.all;
use ieee.numeric_std.all;

entity Register_File is
  port(
    saida_A        : out std_logic_vector(31 downto 0);  -- Saída do registro A
    saida_B        : out std_logic_vector(31 downto 0);  -- Saída do registro B
    RegManual_Out  : out std_logic_vector(31 downto 0);  -- Saída de um registro selecionado manualmente
    input          : in  std_logic_vector(31 downto 0);  -- Dado de entrada para escrever em um registro
    sel_RegManual  : in  std_logic_vector(4 downto 0);   -- Seleção manual de registro de saída
    WriteEnable    : in  std_logic;                      -- Sinal de habilitação de escrita em um registro
    sel_RegA       : in  std_logic_vector(4 downto 0);   -- Seleção do registrador A para leitura
    sel_RegB       : in  std_logic_vector(4 downto 0);   -- Seleção do registrador B para leitura
    sel_WriteReg   : in  std_logic_vector(4 downto 0);   -- Seleção do registrador para escrita
    clk            : in  std_logic                       -- Sinal de clock
    );
end Register_File;

architecture Behavioral of Register_File is

  -- Declaração de um tipo array que representa o banco de registradores com 32 registros de 32 bits cada
  type RegisterFile is array(0 to 31) of std_logic_vector(31 downto 0);
  -- Declaração de um sinal (variável interna) chamado "registers" do tipo registerFile
  signal registers : RegisterFile := 
   ("00000000000000000000000000011111","00000000000000000000000000000001","00000000000000000000000000000000","00000000000000000000000000000000",
    "00000000000000000000000000000000","00000000000000000000000000000000","00000000000000000000000000000000","00000000000000000000000000000000",
    "00000000000000000000000000000000","00000000000000000000000000000000","00000000000000000000000000000000","00000000000000000000000000000000",
    "00000000000000000000000000000000","00000000000000000000000000000000","00000000000000000000000000000000","00000000000000000000000000000000",
    "00000000000000000000000000000000","00000000000000000000000000000000","00000000000000000000000000000000","00000000000000000000000000000000",
    "00000000000000000000000000000000","00000000000000000000000000000000","00000000000000000000000000000000","00000000000000000000000000000000",
    "00000000000000000000000000000000","00000000000000000000000000000000","00000000000000000000000000000000","00000000000000000000000000000000",
    "00000000000000000000000000000000","00000000000000000000000000000000","00000000000000000000000000000000","00000000000000000000000000000000");

begin

  regFile : process (clk) is
  begin
  
    IF rising_edge(clk) THEN
      -- Realiza a leitura dos registradores A e B antes de fazer o bypass
      IF (registers(to_integer(unsigned(sel_RegA))) = "UUUUUUUUUUUUUUUUUUUUUUUUUUUUUUUU") THEN
        saida_A <= (others => '0');  -- Se o registro for inválido (contém "U"), a saída é zerada
      ELSE 
        saida_A <= registers(to_integer(unsigned(sel_RegA)));  -- Caso contrário, a saída é o valor do registrador A
      end IF;
      IF (registers(to_integer(unsigned(sel_RegB))) = "UUUUUUUUUUUUUUUUUUUUUUUUUUUUUUUU") THEN
        saida_B <= (others => '0');  -- Se o registro for inválido (contém "U"), a saída é zerada
      ELSE
        saida_B <= registers(to_integer(unsigned(sel_RegB)));  -- Caso contrário, a saída é o valor do registrador B
      end IF;
      -- Escrita e bypass
      IF WriteEnable = '1' THEN
        -- Se o sinal de escrita estiver habilitado (writeEnable = '1'), então o dado de entrada "input" será escrito no registrador selecionado por "writeRegSel"
        registers(to_integer(unsigned(sel_WriteReg))) <= input;  -- Write
        -- Além disso, é feito o bypass para leitura dos registradores A e B
        IF sel_RegA = sel_WriteReg THEN  -- Bypass para leitura do registrador A
          saida_A <= input;  -- O valor de "input" é direcionado para a saída do registrador A
        end IF;
        IF sel_RegB = sel_WriteReg THEN  -- Bypass para leitura do registrador B
          saida_B <= input;  -- O valor de "input" é direcionado para a saída do registrador B
        end IF;
      end IF;
    end IF;
  end process;
  
  -- seleção manual
  -- Saída de um registrador selecionado manualmente com base no valor de "regSelManual"
  
  RegManual_Out <= registers(to_integer(unsigned(sel_RegManual)));
  
end Behavioral;

// VHDL entity IFID, as the project stores it:
library IEEE;
use IEEE.std_logic_1164.all;

entity IFID is
  port (
    clk            : in  std_logic;                      -- Sinal de clock
    PC_In          : in  std_logic_vector(31 downto 0);  -- PC de entrada (Program Counter)
    PC4_In         : in  std_logic_vector(31 downto 0);  -- PC+4 de entrada (PC + 4)
    instrucao_In   : in  std_logic_vector(31 downto 0);  -- Instrução de entrada
    PC_Out         : out std_logic_vector(31 downto 0);  -- PC de saída (Program Counter)
    PC4_Out        : out std_logic_vector(31 downto 0);  -- PC+4 de saída (PC + 4)
    instrucao_Out  : out std_logic_vector(31 downto 0)   -- Instrução de saída
    );
end IFID;

architecture Behavioral of IFID is

signal reg : std_logic_vector(95 downto 0); -- Registrador interno do estágio IF/ID com 96 bits

begin

	process (clk)
	begin
		IF (rising_edge(clk)) THEN
			-- No pulso de subida do clock, os dados de entrada são armazenados no registrador IDIF
			reg(31 downto 0)  <= instrucao_In;  -- Armazena a instrução
			reg(63 downto 32) <= PC_In;         -- Armazena o PC de entrada
			reg(95 downto 64) <= PC4_In;        -- Armazena o PC+4 de entrada
		end IF;
		IF (falling_edge(clk)) THEN
			-- No pulso de descida do clock, os dados armazenados no registrador IDIF são disponibilizados nas saídas
			PC_Out <= reg(63 downto 32);        -- Fornece o PC de saída
			instrucao_Out <= reg(31 downto 0);  -- Fornece a instrução de saída
			PC4_Out <= reg(95 downto 64);       -- Fornece o PC+4 de saída
		end IF;
	end process;
	
end Behavioral;

// VHDL entity IDEX, as the project stores it:
library IEEE;
use IEEE.std_logic_1164.all;

entity IDEX is
  port (
    clk             : in  std_logic;                      -- Sinal de clock
    PC_In           : in  std_logic_vector(31 downto 0);  -- PC de entrada (Program Counter)
    read1_In        : in  std_logic_vector(31 downto 0);  -- Registrador de leitura 1 de entrada
    read2_In        : in  std_logic_vector(31 downto 0);  -- Registrador de leitura 2 de entrada
    immGen_In       : in  std_logic_vector(31 downto 0);  -- Saída do bloco "ImmGen" (gerador de imediatos) de entrada
    aluControl_In   : in  std_logic_vector(3 downto 0);   -- Controle da ALU (Unidade Lógica e Aritmética) de entrada
    wbAdd_In        : in  std_logic_vector(4 downto 0);   -- Endereço do registrador de escrita de volta de entrada
    WB_In           : in  std_logic_vector(2 downto 0);   -- Controle do estágio de escrita de volta (WB) de entrada
    Mem_in          : in  std_logic_vector(5 downto 0);   -- Controle do estágio de memória (Mem) de entrada
    EX_In           : in  std_logic_vector(6 downto 0);   -- Controle do estágio de execução (EX) de entrada
    PC4_In          : in  std_logic_vector(31 downto 0);  -- PC + 4 de entrada
    PC_Out          : out std_logic_vector(31 downto 0);  -- PC de saída (Program Counter)
    read1_Out       : out std_logic_vector(31 downto 0);  -- Registrador de leitura 1 de saída
    read2_Out       : out std_logic_vector(31 downto 0);  -- Registrador de leitura 2 de saída
    immGen_Out      : out std_logic_vector(31 downto 0);  -- Saída do bloco "ImmGen" (gerador de imediatos) de saída
    aluControl_Out  : out std_logic_vector(3 downto 0);   -- Controle da ALU (Unidade Lógica e Aritmética) de saída
    wbAdd_Out       : out std_logic_vector(4 downto 0);   -- Endereço do registrador de escrita de volta de saída
    WB_Out          : out std_logic_vector(2 downto 0);   -- Controle do estágio de escrita de volta (WB) de saída
    Mem_Out         : out std_logic_vector(5 downto 0);   -- Controle do estágio de memória (Mem) de saída
    EX_Out          : out std_logic_vector(6 downto 0);   -- Controle do estágio de execução (EX) de saída
    PC4_Out         : out std_logic_vector(31 downto 0)   -- PC + 4 de saída
    );
end IDEX;

architecture Behavioral of IDEX is

signal idex_s : std_logic_vector(184 downto 0); -- Registrador interno do estágio IDEX com 185 bits

begin

	process (clk)
	begin
	
		IF (rising_edge(clk)) THEN
			-- No pulso de subida do clock, os dados de entrada são armazenados no registrador idex_s
			idex_s(31 downto 0)    <= PC_In;
			idex_s(63 downto 32)   <= read1_In;
			idex_s(95 downto 64)   <= read2_In;
			idex_s(127 downto 96)  <= immGen_In;
			idex_s(131 downto 128) <= aluControl_In;
			idex_s(136 downto 132) <= wbAdd_In;
			idex_s(139 downto 137) <= WB_In;
			idex_s(145 downto 140) <= Mem_In;
			idex_s(152 downto 146) <= EX_In;
			idex_s(184 downto 153) <= PC4_In;
		end IF;
		IF (falling_edge(clk)) THEN
			-- No pulso de descida do clock, os dados armazenados no registrador idex_s são disponibilizados nas saídas
			PC_Out    <= idex_s(31 downto 0);
			read1_Out <= idex_s(63 downto 32);
			read2_Out <= idex_s(95 downto 64);
			immGen_Out <= idex_s(127 downto 96);
			aluControl_Out <= idex_s(131 downto 128);
			wbAdd_Out <= idex_s(136 downto 132);
			WB_Out <= idex_s(139 downto 137);
			Mem_Out <= idex_s(145 downto 140);
			EX_Out <= idex_s(152 downto 146);
			PC4_Out <= idex_s(184 downto 153);
		end IF;
	end process;
	
END Behavioral;

// VHDL entity EXMEM, as the project stores it:
library IEEE;
use IEEE.std_logic_1164.all;

entity EXMEM is
  port (
    clk           : in  std_logic;                      -- Sinal de clock
    soma_In       : in  std_logic_vector(31 downto 0);  -- Resultado da ALU de entrada
    zero_In       : in  std_logic;                      -- Sinal indicando se a saída da ALU é zero de entrada
    alu_In        : in  std_logic_vector(31 downto 0);  -- Saída da ALU de entrada
    read2_In      : in  std_logic_vector(31 downto 0);  -- Registrador de leitura 2 de entrada
    wbAdd_In      : in  std_logic_vector(4 downto 0);   -- Endereço do registrador de escrita de volta de entrada
    WB_In         : in  std_logic_vector(2 downto 0);   -- Controle do estágio de escrita de volta (WB) de entrada
    Mem_In        : in  std_logic_vector(5 downto 0);   -- Controle do estágio de memória (M) de entrada
    PC4_In        : in  std_logic_vector(31 downto 0);  -- PC + 4 de entrada
    PC_Out        : out std_logic_vector(31 downto 0);  -- PC de saída (Program Counter)
    zero_Out      : out std_logic;                      -- Sinal indicando se a saída da ALU é zero de saída
    alu_Out       : out std_logic_vector(31 downto 0);  -- Saída da ALU de saída
    read2_Out     : out std_logic_vector(31 downto 0);  -- Registrador de leitura 2 de saída
    wbAdd_Out     : out std_logic_vector(4 downto 0);   -- Endereço do registrador de escrita de volta de saída
    WB_out        : out std_logic_vector(2 downto 0);   -- Controle do estágio de escrita de volta (WB) de saída
    Mem_out       : out std_logic_vector(5 downto 0);   -- Controle do estágio de memória (M) de saída
    PC4_Out       : out std_logic_vector(31 downto 0)   -- PC + 4 de saída
    );
end EXMEM;

architecture Behavioral of EXMEM is

signal exmem_s : std_logic_vector(142 downto 0); -- Registrador interno do estágio EXMEM com 143 bits

begin

	process (clk)
	begin
	
		IF (rising_edge(clk)) THEN
			-- No pulso de subida do clock, os dados de entrada são armazenados no registrador exmem_s
			exmem_s(31 downto 0)   <= soma_In;
			exmem_s(32)  <= zero_In;
			exmem_s(64 downto 33)  <= alu_In;
			exmem_s(96 downto 65) <= read2_In;
			exmem_s(101 downto 97) <= wbAdd_In;
			exmem_s(104 downto 102) <= WB_In;
			exmem_s(110 downto 105) <= Mem_In;
			exmem_s(142 downto 111) <= PC4_In;
		end IF;
		IF (falling_edge(clk)) THEN
			-- No pulso de descida do clock, os dados armazenados no registrador exmem_s são disponibilizados nas saídas
			PC_Out <= exmem_s(31 downto 0);
			IF (exmem_s(32) = 'U') THEN
				zero_Out <= '0';
			ELSE
				zero_Out <= exmem_s(32);
			end IF;
			IF (exmem_s(64 downto 33) = "UUUUUUUUUUUUUUUUUUUUUUUUUUUUUUUU") THEN
				alu_Out <= "00000000000000000000000000000000";
			ELSE
				alu_Out <= exmem_s(64 downto 33);
			end IF;
			
			read2_Out <= exmem_s(96 downto 65);
			wbAdd_Out <= exmem_s(101 downto 97);
			
			IF (exmem_s(110 downto 105) = "UUUUUU") THEN
				Mem_Out <= "000000";
			ELSE
				Mem_Out <= exmem_s(110 downto 105);
			end IF;
			
			WB_Out <= exmem_s(104 downto 102);

			PC4_Out <= exmem_s(142 downto 111);
			
			
		end IF;
	end process;
	
end Behavioral;

// VHDL entity MEMWB, as the project stores it:
library IEEE;
use IEEE.std_logic_1164.all;

entity MEMWB is
  port (
    clk           : in  std_logic;                      -- Sinal de clock
    read_In       : in  std_logic_vector(31 downto 0);  -- Dado lido da memória de entrada
    alu_In        : in  std_logic_vector(31 downto 0);  -- Saída da ALU de entrada
    wbAdd_In      : in  std_logic_vector(4 downto 0);   -- Endereço do registrador de escrita de volta de entrada
    WB_In         : in  std_logic_vector(2 downto 0);   -- Controle do estágio de escrita de volta (WB) de entrada
    PC4_In        : in  std_logic_vector(31 downto 0);  -- PC + 4 de entrada
    PCI_In        : in  std_logic_vector(31 downto 0);  -- PC + Instrução de 32 bits de entrada
    read_Out      : out std_logic_vector(31 downto 0);  -- Dado lido da memória de saída
    alu_Out       : out std_logic_vector(31 downto 0);  -- Saída da ALU de saída
    wbAdd_Out     : out std_logic_vector(4 downto 0);   -- Endereço do registrador de escrita de volta de saída
    WB_Out        : out std_logic_vector(2 downto 0);   -- Controle do estágio de escrita de volta (WB) de saída
    PC4_Out       : out std_logic_vector(31 downto 0);  -- PC + 4 de saída
    PCI_Out       : out std_logic_vector(31 downto 0)   -- PC + Instrução de 32 bits de saída
    );
end MEMWB;

architecture Behavioral of MEMWB is

signal memwb_s : std_logic_vector(135 downto 0); -- Registrador interno do estágio MEMWB com 136 bits

begin

	process (clk)
	begin
	
		IF (rising_edge(clk)) THEN
			-- No pulso de subida do clock, os dados de entrada são armazenados no registrador memwb_s
			memwb_s(31 downto 0)   <= read_In;
			memwb_s(63 downto 32)  <= alu_In;
			memwb_s(68 downto 64)  <= wbAdd_In;
			memwb_s(71 downto 69)  <= WB_In;
			memwb_s(103 downto 72) <= PC4_In;
			memwb_s(135 downto 104) <= PCI_In;	
		end IF;
		IF (falling_edge(clk)) THEN
			-- No pulso de descida do clock, os dados armazenados no registrador memwb_s são disponibilizados nas saídas
			read_Out  <=  memwb_s(31 downto 0);
			alu_Out   <=  memwb_s(63 downto 32);
			wbAdd_Out <= memwb_s(68 downto 64);
			WB_Out  <= memwb_s(71 downto 69);
			PC4_Out <= memwb_s(103 downto 72);
			PCI_Out <= memwb_s(135 downto 104);
		end IF;
	end process;
	
end Behavioral;
